# Fritzing sketch fritzing_electronics2 (saved by Fritzing 0.9.4)
breadboards: 2

parts:
  M15 = DC Motor
  M16 = DC Motor
  M17 = DC Motor
  M18 = DC Motor
  M19 = DC Motor
  M20 = DC Motor
  Mod1 = Raspberry Pi 4B
  Hybrid_Circuit1 = JY-MCU 3V-5V Bidirectional Level Shifter [package="DIP (Dual Inline)"]
  Part6 = Arduino Leonardo (Rev3b)
  Part7 = HX711 Weighing Sensor Module
  Part8 = HX711 Weighing Sensor Module
  Part9 = HX711 Weighing Sensor Module
  Part11 = HX711 Weighing Sensor Module
  Part12 = HX711 Weighing Sensor Module
  Part13 = HX711 Weighing Sensor Module
  DS1 = DS18B20 1-Wire Temperature Sensor [part_number=DS18B20]
  R1 = Resistor [tolerance=±5% resistance=220 package="1206 [SMD]"]  # not connected
  ENCODER1 = Rotary Encoder with switch (KY-040) [part_number=KY-040]
  LCD1 = LCD screen
  U3 = POT [package=pot_mammoth]
  V1 = DC Power [voltage=5]

nets (from the schematic view):
  N1: M15.pin_1, Part6.D5_PWM
  N2: M16.pin_1, Part6.D7
  N3: M16.pin_2, M18.pin_2
  N4: M17.pin_1, Part6.D3_PWM/SCL
  GND: M17.pin_2, M19.pin_2, Mod1.GND, DS1.GND
  N5: M18.pin_1, Part6.D2/SDA, Part6.SDA
  N6: M19.pin_1, Part6.D4/A6
  N7: M20.pin_1, Part6.D6_PWM/A7
  3V3: Mod1.3V3, DS1.VDD
  N8: Mod1.GPIO14, Hybrid_Circuit1.I/O-1H
  N9: Mod1.GPIO15, Hybrid_Circuit1.I/O-2H
  N10: Mod1.GPIO18, LCD1.DB7
  N11: Mod1.GPIO23, LCD1.DB6
  N12: Mod1.GPIO24, LCD1.DB5
  N13: Mod1.GPIO13, LCD1.DB4
  N14: Mod1.GPIO19, LCD1.E
  N15: Mod1.GPIO16, ENCODER1.SW
  N16: Mod1.GPIO26, LCD1.RS
  N17: Mod1.GPIO20, ENCODER1.DT
  N18: Mod1.GPIO21, ENCODER1.CLK
  N19: Hybrid_Circuit1.3.3Vout, LCD1.VDD, LCD1.LED+, U3.A, V1.V+
  N20: Hybrid_Circuit1.GND#1, Part6.GND
  N21: Hybrid_Circuit1.I/O-1L, Part6.D0/RX
  N22: Hybrid_Circuit1.I/O-2L, Part6.D1/TX
  VCC: Hybrid_Circuit1.5Vin, Part6.5V, Part8.VCC, Part9.VCC, Part11.VCC, Part12.VCC, Part13.VCC
  N23: Part6.A0, Part13.DO/RX
  N24: Part6.A1, Part12.DO/RX
  N25: Part6.A2, Part11.DO/RX
  N26: Part6.A3, Part9.DO/RX
  N27: Part6.A4, Part8.DO/RX
  N28: Part6.A5, Part7.DO/RX
  N29: Part6.D9_PWM/A9, Part8.CK/TX, Part9.CK/TX, Part13.CK/TX
  GND_2: Part7.GND, Part8.GND, Part9.GND, Part11.GND, Part12.GND, Part13.GND, LCD1.VSS, LCD1.R/W, LCD1.LED-, U3.E, V1.V-
  N30: ENCODER1.GND, ENCODER1.+
  N31: LCD1.V0, U3.S

custom parts:
  JY-MCU 3V-5V Bidirectional Level Shifter: JY-MCU 3V-5V Bidirectional Level Shifter with 12 pins on a 500mil dual inline package (DIP) footprint.
  Rotary Encoder with switch (KY-040): A Rotary Encoder with switch
